# Fritzing sketch full ir system 2 (saved by Fritzing 0.9.3b)
circuit board: 8.46667cm x 5.64444cm
breadboards: 1

parts:
  Part1 = Arduino Uno (Rev3)
  D1 = LTE-302 [package=lte-302]
  Part2 = Bluetooth HC-05 Macho
  R1 = Resistor [tolerance=±5% resistance=220 package="0603 [SMD]"]
  IR2 = TSOP312.., 314.. [package=THT]
  R3 = Resistor [tolerance=±5% resistance=47 package="0603 [SMD]"]
  R4 = Resistor [tolerance=±5% resistance=22k package="0603 [SMD]"]
  C2 = Capacitor Polarized [package=cpol-radial-100uf-25v]

nets:
  N1: Part1.D8, Part2.RXD
  N2: Part1.D11_PWM/MOSI, IR2.GND, R4.Pin_1
  GND: Part1.GND, D1.C, Part2.GND, IR2.Vs, C2.-
  N3: Part1.D3_PWM, R1.Pin_0
  N4: Part1.D7, Part2.TXD
  3V3: Part1.3V3, Part2.VCC
  N5: Part1.5V, R3.Pin_0, R4.Pin_0
  N6: D1.A, R1.Pin_1
  N7: IR2.Data, R3.Pin_1, C2.+
