# Fritzing sketch full ir system (saved by Fritzing 0.9.3b)
circuit board: 8.46667cm x 5.64444cm
breadboards: 1

parts:
  Part1 = Arduino Uno (Rev3)
  D1 = LTE-302 [package=lte-302]
  Part2 = Bluetooth HC-05 Macho
  R1 = Resistor [tolerance=±5% resistance=220 package="0603 [SMD]"]

nets:
  N1: Part1.D8, Part2.RXD
  GND: Part1.GND, D1.C, Part2.GND
  N2: Part1.D3_PWM, R1.Pin_0
  N3: Part1.D7, Part2.TXD
  3V3: Part1.3V3, Part2.VCC
  N4: D1.A, R1.Pin_1
