# Fritzing sketch ir sketch (saved by Fritzing 0.9.3b)
breadboards: 1

parts:
  Part1 = Arduino Uno (Rev3)
  IR1 = TSOP312.., 314.. [package=THT]

nets:
  N1: Part1.D11_PWM/MOSI, IR1.GND
  N2: Part1.GND, IR1.Vs
  N3: Part1.5V, IR1.Data
