# Fritzing sketch smoothing sketch (saved by Fritzing 0.9.3b)
breadboards: 1

parts:
  Part1 = Arduino Uno (Rev3)
  IR1 = TSOP312.., 314.. [package=THT]
  C1 = Capacitor Polarized [package=cpol-radial-100uf-25v]
  R1 = Resistor [tolerance=±5% resistance=47 package="0603 [SMD]"]
  R2 = Resistor [tolerance=±5% resistance=22k package="0603 [SMD]"]

nets:
  N1: Part1.D11_PWM/MOSI, IR1.GND, R2.Pin_1
  N2: Part1.GND, IR1.Vs, C1.-
  N3: Part1.5V, R1.Pin_0, R2.Pin_0
  N4: IR1.Data, C1.+, R1.Pin_1
